// Logisim project 2digitcounter.circ as structural Verilog: 4 circuits, main circuit main
module main (
  input  in_1
);

  wire counter1_a, counter1_b, counter1_c, counter1_d, counter1_output_counter_2, counter2_a, counter2_b,
       counter2_c, counter2_d, decoder_2_a_2, decoder_2_b_2, decoder_2_c_2, decoder_2_d_2, decoder_2_e,
       decoder_2_f, decoder_2_g, decoder_a_2, decoder_b_2, decoder_c_2, decoder_d_2, decoder_e, decoder_f,
       decoder_g;

  counter2 counter2 (
    .in_1(in_1), .in_2(counter1_output_counter_2), .d(counter2_d), .c(counter2_c), .b(counter2_b),
    .a(counter2_a));  // open: out_3
  counter1 counter1 (
    .in_1(in_1), .d(counter1_d), .c(counter1_c), .b(counter1_b), .a(counter1_a),
    .output_counter_2(counter1_output_counter_2));
  decoder decoder (
    .A(counter2_d), .B(counter2_c), .C(counter2_b), .D(counter2_a), .a_2(decoder_a_2), .b_2(decoder_b_2),
    .e(decoder_e), .c_2(decoder_c_2), .f(decoder_f), .d_2(decoder_d_2), .g(decoder_g));
  decoder decoder_2 (
    .A(counter1_d), .B(counter1_c), .C(counter1_b), .D(counter1_a), .a_2(decoder_2_a_2), .b_2(decoder_2_b_2),
    .e(decoder_2_e), .c_2(decoder_2_c_2), .f(decoder_2_f), .d_2(decoder_2_d_2), .g(decoder_2_g));
  _7_Segment_Display u_7_segment_display_1 (
    .g(decoder_d_2), .f(decoder_c_2), .a(decoder_b_2), .b(decoder_a_2), .e(decoder_g), .d(decoder_f),
    .c(decoder_e));  // open: dp
  _7_Segment_Display u_7_segment_display_2 (
    .g(decoder_2_d_2), .f(decoder_2_c_2), .a(decoder_2_b_2), .b(decoder_2_a_2), .e(decoder_2_g),
    .d(decoder_2_f), .c(decoder_2_e));  // open: dp

  // Notes on the sheet:
  //   digital display
endmodule

module decoder (
  input  A,
  input  B,
  input  C,
  input  D,
  output a_2,
  output b_2,
  output e,
  output c_2,
  output f,
  output d_2,
  output g
);

  wire and_1_out, and_2_out, and_3_out, and_4_out, and_5_out, and_6_out, and_7_out, and_8_out, and_9_out,
       and_10_out, and_11_out, and_12_out, and_13_out, and_14_out, and_15_out, and_16_out, not_1_out,
       not_2_out, not_3_out, not_4_out, not_5_out, not_6_out, not_7_out, not_8_out, not_9_out, not_10_out,
       not_11_out, not_12_out, not_13_out, not_14_out, not_15_out, not_16_out, not_17_out, not_18_out,
       not_19_out, not_20_out, not_21_out;

  not not_1 (not_1_out, B);
  not not_2 (not_2_out, C);
  and and_1 (and_1_out, not_2_out, not_3_out);
  not not_3 (not_3_out, D);
  and and_2 (and_2_out, C, D);
  not not_4 (not_4_out, B);
  and and_3 (and_3_out, not_4_out, not_5_out);
  not not_5 (not_5_out, D);
  and and_4 (and_4_out, B, D);
  not not_6 (not_6_out, C);
  or or_1 (e, not_6_out, D, B);
  not not_7 (not_7_out, C);
  and and_5 (and_5_out, not_7_out, not_8_out);
  not not_8 (not_8_out, D);
  and and_6 (and_6_out, B, not_9_out);
  not not_9 (not_9_out, C);
  and and_7 (and_7_out, B, not_10_out);
  not not_10 (not_10_out, D);
  not not_11 (not_11_out, B);
  and and_8 (and_8_out, not_11_out, not_12_out);
  not not_12 (not_12_out, D);
  not not_13 (not_13_out, B);
  and and_9 (and_9_out, not_13_out, C);
  and and_10 (and_10_out, C, not_14_out);
  not not_14 (not_14_out, D);
  not not_15 (not_15_out, C);
  and and_11 (and_11_out, B, not_15_out, D);
  not not_16 (not_16_out, B);
  and and_12 (and_12_out, not_16_out, C);
  and and_13 (and_13_out, B, not_17_out);
  not not_17 (not_17_out, C);
  and and_14 (and_14_out, B, not_18_out);
  not not_18 (not_18_out, D);
  not not_19 (not_19_out, B);
  and and_15 (and_15_out, not_19_out, not_20_out);
  not not_20 (not_20_out, D);
  and and_16 (and_16_out, C, not_21_out);
  not not_21 (not_21_out, D);
  or or_2 (a_2, not_1_out, and_1_out, and_2_out);
  or or_3 (b_2, and_3_out, C, and_4_out, A);
  or or_4 (c_2, and_5_out, and_6_out, and_7_out, A);
  or or_5 (f, and_8_out, and_9_out, and_10_out, and_11_out, A);
  or or_6 (d_2, and_12_out, and_13_out, and_14_out, A);
  or or_7 (g, and_15_out, and_16_out);
  _7_Segment_Display u_7_segment_display_1 (.g(d_2), .f(c_2), .a(b_2), .b(a_2), .e(g), .d(f), .c(e));  // open: dp
endmodule

module counter1 (
  input  in_1,
  output output_counter_2,
  output d,
  output c,
  output b,
  output a
);

  wire and_1_out, clock_1_out, j_k_ff_1_qn, j_k_ff_2_qn, j_k_ff_3_qn;

  Clock clock_1 (.out(clock_1_out));
  and and_1 (and_1_out, d, b);
  J_K_Flip_Flop j_k_ff_1 (
    .J(in_1), .clk(clock_1_out), .K(in_1), .Q(a), .Qn(j_k_ff_1_qn), .reset(and_1_out));  // open: preset, en
  J_K_Flip_Flop j_k_ff_2 (
    .J(in_1), .clk(j_k_ff_1_qn), .K(in_1), .Q(b), .Qn(j_k_ff_2_qn), .reset(and_1_out));  // open: preset, en
  J_K_Flip_Flop j_k_ff_3 (
    .J(in_1), .clk(j_k_ff_2_qn), .K(in_1), .Q(c), .Qn(j_k_ff_3_qn), .reset(and_1_out));  // open: preset, en
  J_K_Flip_Flop j_k_ff_4 (
    .J(in_1), .clk(j_k_ff_3_qn), .K(in_1), .Q(d), .Qn(output_counter_2), .reset(and_1_out));  // open: preset, en

  // Notes on the sheet:
  //   COUNTER 1
endmodule

module counter2 (
  input  in_1,
  input  in_2,
  output out_3,
  output d,
  output c,
  output b,
  output a
);

  wire and_1_out, j_k_ff_1_qn, j_k_ff_2_qn, j_k_ff_3_qn;

  and and_1 (and_1_out, d, b);
  J_K_Flip_Flop j_k_ff_1 (
    .J(in_1), .clk(in_2), .K(in_1), .Q(a), .Qn(j_k_ff_1_qn), .reset(and_1_out));  // open: preset, en
  J_K_Flip_Flop j_k_ff_2 (
    .J(in_1), .clk(j_k_ff_1_qn), .K(in_1), .Q(b), .Qn(j_k_ff_2_qn), .reset(and_1_out));  // open: preset, en
  J_K_Flip_Flop j_k_ff_3 (
    .J(in_1), .clk(j_k_ff_2_qn), .K(in_1), .Q(c), .Qn(j_k_ff_3_qn), .reset(and_1_out));  // open: preset, en
  J_K_Flip_Flop j_k_ff_4 (
    .J(in_1), .clk(j_k_ff_3_qn), .K(in_1), .Q(d), .Qn(out_3), .reset(and_1_out));  // open: preset, en

  // Notes on the sheet:
  //   COUNTER 2
endmodule
